# Fritzing sketch circuit (saved by Fritzing 0.9.3b)
breadboards: 1

parts:
  U1 = LuaNode32 / ESP32
  부품1 = Soil Moisture Sensor

nets:
  N1: U1.D32, 부품1.SIG
  3V3: U1.3V3, 부품1.VCC
  GND: U1.GND, 부품1.GND

custom parts:
  LuaNode32 / ESP32: ESP32 based LuaNode32
